# Fritzing sketch final board (saved by Fritzing 0.9.3b)
circuit board: 16cm x 14cm
breadboards: 1

parts:
  Arduino_Due = Arduino Due (Rev2b)
  X-_Axis = DRV 8825 Stepper Motor Carrier, High Current [part_number="DRV 8825"]
  Z-_Axis = DRV 8825 Stepper Motor Carrier, High Current [part_number="DRV 8825"]
  Y-_Axis = DRV 8825 Stepper Motor Carrier, High Current [part_number="DRV 8825"]
  Y'-_Axis = DRV 8825 Stepper Motor Carrier, High Current [part_number="DRV 8825"]
  P1 = Power plug
  P2 = Power plug
  CX = Electrolytic Capacitor [capacitance=0.1mF voltage=35V package="100 mil [THT, electrolytic]"]
  CZ = Electrolytic Capacitor [capacitance=0.1mF voltage=35V package="100 mil [THT, electrolytic]"]
  2A_2B = Battery
  1A_1B = Battery
  2A_2B_2 = Battery
  1A_1B_2 = Battery
  2A_2B_3 = Battery
  1A_1B_3 = Battery
  1A_1B_4 = Battery
  2A_2B_4 = Battery
  CY' = Electrolytic Capacitor [capacitance=0.1mF voltage=35V package="100 mil [THT, electrolytic]"]
  CY = Electrolytic Capacitor [capacitance=0.1mF voltage=35V package="100 mil [THT, electrolytic]"]
  F2 = Battery
  F1 = Battery
  F3 = Battery
  F5 = Battery
  F4 = Battery
  F6 = Battery
  F7 = Battery
  X- = Battery
  X+ = Battery
  Y- = Battery
  Y+ = Battery
  Z- = Battery
  Z+ = Battery
  XM1 = Battery
  M2 = Battery
  M3 = Battery
  YM1 = Battery
  M2_2 = Battery
  M3_2 = Battery
  M3_3 = Battery
  ZM1 = Battery
  M2_3 = Battery

nets:
  N1: Arduino_Due.IOREF, X-_Axis.VOLTAGE_DD, Z-_Axis.VOLTAGE_DD, Y-_Axis.VOLTAGE_DD, Y'-_Axis.VOLTAGE_DD
  GND: Arduino_Due.GND, X-_Axis.GROUND_ST/_MT, X-_Axis.GROUND_LOG, Z-_Axis.GROUND_ST/_MT, Z-_Axis.GROUND_LOG, Y-_Axis.GROUND_ST/_MT, Y-_Axis.GROUND_LOG, Y'-_Axis.GROUND_ST/_MT, Y'-_Axis.GROUND_LOG, P1.GND, P2.GND, CX.-, CZ.-, CY'.-, CY.-, F2.-, F1.-, F3.-, F5.-, F4.-, F6.-, F7.-, X-.+, X+.+, Y-.+, Y+.+, Z-.+, Z+.+
  N2: Arduino_Due.D8_PWM, X-_Axis.ENABLE, Z-_Axis.ENABLE, Y-_Axis.ENABLE, Y'-_Axis.ENABLE
  N3: Arduino_Due.D2_PWM, Z-_Axis.DIRECTION
  N4: Arduino_Due.D3_PWM, Z-_Axis.STEP
  N5: Arduino_Due.D4_PWM/SS1, Y-_Axis.DIRECTION, Y'-_Axis.DIRECTION
  N6: Arduino_Due.D5_PWM, Y-_Axis.STEP, Y'-_Axis.STEP
  N7: Arduino_Due.D6_PWM, X-_Axis.DIRECTION
  N8: Arduino_Due.D7_PWM, X-_Axis.STEP
  N9: Arduino_Due.D37, ZM1.+
  N10: Arduino_Due.D39, M2_3.+
  N11: Arduino_Due.D41, M3_3.+
  N12: Arduino_Due.D42, M3_2.+
  N13: Arduino_Due.D43, Z-.-
  N14: Arduino_Due.D44, M2_2.+
  N15: Arduino_Due.D45, Z+.-
  N16: Arduino_Due.D46, YM1.+
  N17: Arduino_Due.D47, Y-.-
  N18: Arduino_Due.D48, M3.+
  N19: Arduino_Due.D49, Y+.-
  N20: Arduino_Due.D50, M2.+
  N21: Arduino_Due.D51, X-.-
  N22: Arduino_Due.D52, XM1.+
  N23: Arduino_Due.D53, X+.-
  N24: X-_Axis.MS1, XM1.-
  N25: X-_Axis.MS2, M2.-
  N26: X-_Axis.MS3, M3.-
  N27: X-_Axis.RESET, X-_Axis.SLEEP
  N28: X-_Axis.VOLTAGE_ST/_MT, Z-_Axis.VOLTAGE_ST/_MT, P1.VCC, CX.+, CZ.+, F2.+, F1.+, F3.+
  N29: X-_Axis.OUT_2B, 2A_2B.-
  N30: X-_Axis.OUT_2A, 2A_2B.+
  N31: X-_Axis.OUT_1A, 1A_1B.-
  N32: X-_Axis.OUT_1B, 1A_1B.+
  N33: Z-_Axis.MS1, ZM1.-
  N34: Z-_Axis.MS2, M2_3.-
  N35: Z-_Axis.MS3, M3_3.-
  N36: Z-_Axis.RESET, Z-_Axis.SLEEP
  N37: Z-_Axis.OUT_2B, 2A_2B_2.-
  N38: Z-_Axis.OUT_2A, 2A_2B_2.+
  N39: Z-_Axis.OUT_1A, 1A_1B_2.-
  N40: Z-_Axis.OUT_1B, 1A_1B_2.+
  N41: Y-_Axis.MS1, Y'-_Axis.MS1, YM1.-
  N42: Y-_Axis.MS2, Y'-_Axis.MS2, M2_2.-
  N43: Y-_Axis.MS3, Y'-_Axis.MS3, M3_2.-
  N44: Y-_Axis.RESET, Y-_Axis.SLEEP
  N45: Y-_Axis.VOLTAGE_ST/_MT, Y'-_Axis.VOLTAGE_ST/_MT, P2.VCC, CY'.+, CY.+, F5.+, F4.+, F6.+, F7.+
  N46: Y-_Axis.OUT_2B, 2A_2B_3.-
  N47: Y-_Axis.OUT_2A, 2A_2B_3.+
  N48: Y-_Axis.OUT_1A, 1A_1B_3.-
  N49: Y-_Axis.OUT_1B, 1A_1B_3.+
  N50: Y'-_Axis.RESET, Y'-_Axis.SLEEP
  N51: Y'-_Axis.OUT_2B, 1A_1B_4.-
  N52: Y'-_Axis.OUT_2A, 1A_1B_4.+
  N53: Y'-_Axis.OUT_1A, 2A_2B_4.-
  N54: Y'-_Axis.OUT_1B, 2A_2B_4.+

notes:
  1
  4
  11
  12
  14
  2
  3
  5
  6
  7
  8
  9
  10
  13
  15
  16
  17
  18
  19
  20
  21
  22
  23
  24
  25
  26
  27
  28
  29
  30
  31
